# Fritzing sketch cf-thermostat-esp01 (saved by Fritzing 0.8.7b)
circuit board: 7.67345cm x 2.83419cm
breadboards: 1

parts:
  Part1 = FTDI Basic Programmer
  DHT11_1 = DHT11 module
  U1 = ESP8266 WiFi Module [part_number=ESP8266]

nets:
  N1: Part1.RXI, U1.TXD
  N2: Part1.TXO, U1.RXD
  VCC: Part1.POWER, DHT11_1.VCC, U1.VCC, U1.CH_PD
  GND: Part1.GND, DHT11_1.GND, U1.GND
  N3: DHT11_1.DATA, U1.GPIO_2

notes:
  3.3v

custom parts:
  DHT11 module: DHT11 black pcb module
  ESP8266 WiFi Module: Generic WiFi Module based on the ESP8266 with onboard PCB antenna and UART communications
