# Fritzing sketch cf-thermostat-nodemcu (saved by Fritzing 0.8.7b)

parts:
  DHT11_1 = DHT11 module
  U2 = NodeMCU V3.0
  OLED_I2C1 = OLED 128x64 I2C Monochrome Display

nets:
  VCC: DHT11_1.VCC, U2.Vin
  GND: DHT11_1.GND, U2.GND, OLED_I2C1.GND
  N1: DHT11_1.DATA, U2.D4
  N2: U2.D1, OLED_I2C1.SCK
  N3: U2.D2, OLED_I2C1.SDA
  3V3: U2.3V3, OLED_I2C1.VDD

custom parts:
  DHT11 module: DHT11 black pcb module
  NodeMCU V3.0: ESP8266 based NodeMCU
